# Fritzing sketch Jarvis-1.0 (saved by Fritzing 0.9.10b)
breadboards: 1

parts:
  Part1 = Arduino Uno (Rev3)
  Driver1 = 28BYJ-48 Driver Module [part_number=ULN2003 package=THT]
  SM1 = 28BYJ-48 Stepper Motor [part_number=28BYJ-48]  # not connected
  Mod1 = KY-023 Dual Axis Joystick Module [package="Breakout board"]
  LED1 = smd LED [color="Red (633nm)" package="0805 [SMD]"]
  M3 = Dagu DGServo 9g (Top view) [part_number=RS001B]
  Part3 = Arduino Prototyping Shield
  M4 = Dagu DGServo 9g (Top view) [part_number=RS001B]
  LED2 = smd LED [color="Red (633nm)" package="1206 [SMD]"]  # not connected
  LED3 = smd LED [color="Green (555nm)" package="1206 [SMD]"]  # not connected
  LED4 = smd LED [color="Red (633nm)" package="1206 [SMD]"]  # not connected
  LED5 = smd LED [color="Green (555nm)" package="1206 [SMD]"]  # not connected

nets:
  N1: Part1.D13/SCK, LED1.anode
  N2: Part1.GND, LED1.cathode
  N3: Driver1.IN1, Part3.D2
  N4: Driver1.IN2, Part3.D3
  N5: Driver1.IN3, Part3.D4
  N6: Driver1.IN4, Part3.D5
  GND: Driver1.GND, Mod1.GND, M3.gnd, Part3.GND, M4.gnd
  +5V: Driver1.Vmotor, Mod1.+5V, M3.vcc, Part3.+5V
  N7: Mod1.VRx, Part3.A1
  N8: Mod1.VRy, Part3.A0
  N9: Mod1.SW, Part3.D11
  N10: M3.pulse, Part3.D7

custom parts:
  28BYJ-48 Driver Module: ULN2003 Driver Module for the 28BYJ-48 Unipolar Stepper Motor LED A - Blue wire - Bottom coil left LED B - Pink wire - Top coil left LED C - Yellow wire - Bottom coil right LED D - Orange wire - Top coil right Common rail - red Connector pins: blue - pink - yellow - orange - red Control pins - IN1 to IN4 Power pins - GND & Vmotor (5-12V) On/Off jumper (if removed, power to motor is cut).
  28BYJ-48 Stepper Motor: Unipolar Stepper Motor 28BYJ-48 Top coil - pink & orange Bottom coil - blue & yellow Common rail - red Connector pins: blue - pink - yellow - orange - red
  KY-023 Dual Axis Joystick Module: KY-023 Dual-Axis Joystick Module.
